# Fritzing sketch MIPS (saved by Fritzing 1.0.2b)
circuit board: 8.46667cm x 5.64444cm

parts:
  Arduino_NANO = Arduino Nano (Rev3.0) (ICSP)
  Lm35 = LM35 Temperature Sensor [package="TO92 [THT]"]
  R1 = Resistor [tolerance=±5% resistance=100 package="2010 [SMD]"]  # not connected
  Buzzer = Piezo Speaker  # not connected
  Push_Input = Pushbutton [package="[SMD]"]
  BAT1 = Battery Holders [package=lipo-1100mAh]
  ML8511 = ML8511 UV Sensor Breakout [part_number=SEN-12705]
  OLED = OLED 128x64 I2C Monochrome Display
  BAT2 = Battery Holders [package=lipo-1100mAh]
  MAX30102 = MakerFocus MAX30102
  R2 = Resistor [tolerance=±5% resistance=100 package="2010 [SMD]"]  # not connected
  R3 = Resistor [tolerance=±5% resistance=180 package="2010 [SMD]"]  # not connected
  R4 = Resistor [tolerance=±5% resistance=100 package="2010 [SMD]"]  # not connected
  R5 = Resistor [tolerance=±5% resistance=100 package="2010 [SMD]"]  # not connected
  R6 = Resistor [tolerance=±5% resistance=180 package="2010 [SMD]"]  # not connected
  KY009 = RGB LED (com. cathode, rgb) [color="Red (633nm)" current=0.030A package="5 mm [THT]"]
  KY10 = RGB LED (com. cathode, rgb) [color="Red (633nm)" current=0.030A package="5 mm [THT]"]
  Cancel_button = SWITCH-MOMENTARY-2 [package=tactile-pth]  # not connected

nets:
  GND: Arduino_NANO.GND, Lm35.GND, KY009.common_cathode, KY10.common_cathode
  N1: Arduino_NANO.VIN, Push_Input.Pin_3, Push_Input.Pin_4, BAT1.+
  N2: Arduino_NANO.5V, Lm35.+Vs
  N3: Arduino_NANO.A6, Lm35.Vout
  N4: Arduino_NANO.A1, ML8511.EN
  N5: BAT1.-, BAT2.+
  N6: OLED.SDA, MAX30102.SDA

custom parts:
  ML8511 UV Sensor Breakout: Description: The ML8511 breakout is an easy to use ultraviolet light sensor. The MP8511 UV Sensor works by outputing an analog signal in relation to the amount of UV light it detects. This breakout can be very handy in creating devices that warn the user of sunburn or detect the UV index as it relates to weather conditions. This sensor breakout can detect 280-390nm light most effectively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
  MakerFocus MAX30102: Oximeter module using the MAX30102 chip. As usual, if you want the mounting holes in pcb, you need to drag a hole over the pad in silkscreen to actually drill the hole (by default they are not drilled)
